# Fritzing sketch meteoscheme (saved by Fritzing 0.9.3b)
breadboards: 1

parts:
  Part1 = Arduino Uno (Rev3)
  LCD1 = LCD screen
  LCM1602_IIC1 = LCM1602 IIC [part_number="LCM1602 IIC" chip_label="LCM1602 IIC" package="DIP (Dual Inline) [THT]"]
  BMP280_Breakout1 = BMP280 Breakout Board [part_number=BMP280]
  DHT1 = DHT11 Humitidy and Temperature Sensor
  LED1 = RGB LED (com. cathode, rgb) [package="5 mm [THT]"]
  R2 = Resistor [tolerance=±5% resistance=220 package=THT]
  R4 = Resistor [tolerance=±5% resistance=220 package=THT]
  S1 = Pushbutton [package="[THT]"]
  Part2 = Bluetooth HC-05 Macho  # not connected
  R5 = Resistor [tolerance=±5% resistance=220 package=THT]
  R1 = Resistor [tolerance=±5% resistance=4.7k package=THT]

nets:
  N1: Part1.D10_PWM/SS, BMP280_Breakout1.CSB
  N2: Part1.D11_PWM/MOSI, BMP280_Breakout1.SDA
  N3: Part1.D12/MISO, BMP280_Breakout1.SDO
  N4: Part1.D13/SCK, BMP280_Breakout1.SCL
  N5: Part1.A4/SDA, LCM1602_IIC1.VCC
  N6: Part1.A5/SCL, LCM1602_IIC1.GND
  N7: Part1.D2, S1.Pin_1, S1.Pin_2
  N8: Part1.D3_PWM, R4.Pin_0
  N9: Part1.D5_PWM, R5.Pin_0
  N10: Part1.D6_PWM, R2.Pin_0
  N11: Part1.D7, DHT1.DATA, R1.Pin_1
  3V3: Part1.3V3, BMP280_Breakout1.VCC
  5V: Part1.5V, LCM1602_IIC1.SDA, DHT1.VDD, LED1.green_anode, R1.Pin_0
  GND: Part1.GND, LCM1602_IIC1.SCL, BMP280_Breakout1.GND, DHT1.GND, S1.Pin_3, S1.Pin_4
  VSS: LCD1.VSS, LCM1602_IIC1.VSS
  VDD: LCD1.VDD, LCM1602_IIC1.VDD
  N12: LCD1.V0, LCM1602_IIC1.V0
  N13: LCD1.RS, LCD1.R/W, LCD1.E, LCD1.DB0, LCD1.DB1, LCM1602_IIC1.RS, LCM1602_IIC1.RW, LCM1602_IIC1.E, LCM1602_IIC1.D0, LCM1602_IIC1.D1
  N14: LCD1.DB2, LCM1602_IIC1.D2
  N15: LCD1.DB3, LCM1602_IIC1.D3
  N16: LCD1.DB4, LCM1602_IIC1.D4
  N17: LCD1.DB5, LCM1602_IIC1.D5
  N18: LCD1.DB6, LCM1602_IIC1.D6
  N19: LCD1.DB7, LCM1602_IIC1.D7
  N20: LCD1.LED+, LCM1602_IIC1.A
  N21: LCD1.LED-, LCM1602_IIC1.K
  N22: LED1.red_anode, R2.Pin_1
  N23: LED1.common_cathode, R5.Pin_1
  N24: LED1.blue_anode, R4.Pin_1

custom parts:
  LCM1602 IIC: I2C-Module to use a 1602 or 2004 LCD on with the wire.h libory Serial LCD Modul
  BMP280 Breakout Board: This is a breakout board for the Bosch Sensortec BMP280, "an absolute barometric pressure sensor especially designed for mobile applications." The operation range is 300 to 1100 hPa. Supply voltage is 1.2 to 3.6V. Operating temperature range is -40 to +85 °C.
  DHT11 Humitidy and Temperature Sensor: DHT11 Humidity and Temperature Sensor
